# Fritzing sketch autodigimin (saved by Fritzing 1.0.4)
breadboards: 1

parts:
  Part1 = Mono Audio Amp Breakout  # not connected
  X9C1 = X9C103 digital potentiometer
  SPKR1 = Loudspeaker  # not connected
  HC-SR04_Sensor_1 = HC-SR04 Ultrasonic Distance Sensor
  HC-SR04_Sensor_2 = HC-SR04 Ultrasonic Distance Sensor
  MH-ET_LIVE_ESP32_DEVKIT1 = MH-ET LIVE ESP32 DEVKIT 38 pins

nets:
  VCC: X9C1.VCC, MH-ET_LIVE_ESP32_DEVKIT1.5V
  GND: X9C1.GND, HC-SR04_Sensor_1.GND, MH-ET_LIVE_ESP32_DEVKIT1.GND#70
  N1: X9C1.INC, MH-ET_LIVE_ESP32_DEVKIT1.IO17
  N2: X9C1.U/D, MH-ET_LIVE_ESP32_DEVKIT1.IO18
  N3: X9C1.CS, MH-ET_LIVE_ESP32_DEVKIT1.IO19
  VCC_2: HC-SR04_Sensor_1.VCC, HC-SR04_Sensor_2.VCC, MH-ET_LIVE_ESP32_DEVKIT1.3V3
  N4: HC-SR04_Sensor_1.TRIG, MH-ET_LIVE_ESP32_DEVKIT1.IO15
  N5: HC-SR04_Sensor_1.ECHO, MH-ET_LIVE_ESP32_DEVKIT1.IO16
  N6: HC-SR04_Sensor_2.TRIG, MH-ET_LIVE_ESP32_DEVKIT1.IO22
  N7: HC-SR04_Sensor_2.ECHO, MH-ET_LIVE_ESP32_DEVKIT1.IO23
  N8: HC-SR04_Sensor_2.GND, MH-ET_LIVE_ESP32_DEVKIT1.GND#58

custom parts:
  Mono Audio Amp Breakout: Description: This tiny audio amplifier is based on the Texas Instruments TPA2005D1. Its efficient class-D operation means low heat and long battery life. It can drive an 8-Ohm speaker at up to 1.4 Watts; it won't shake a stadium, but it will provide plenty of volume for your audio projects. The fully-differential inputs are safe for floating audio signals such as from our MP3 Shield, and can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
  X9C103 digital potentiometer: digital potentiometer X9C102 X9C103 X9C103 X9C503
  MH-ET LIVE ESP32 DEVKIT 38 pins: http://mh.nodebb.com/topic/2/mh-et-live-esp32-devkit
